# Fritzing sketch serial-spy (saved by Fritzing 0.9.0b)

parts:
  Composant1 = Arduino Mega 2560 (Rev3)
  Composant2 = Bluetooth Mate Silver

nets:
  N1: Composant1.D19/RX1, Composant2.TX_5V
  GND: Composant1.GND, Composant2.GND

notes:
  Rx
  Tx
  GND
